// Logisim project FinalProject.circ as structural Verilog: 1 circuit, main circuit main
module main (
  input  Manual_cycle,
  input  Reset
);

  wire Goto_enable, main_2_alu_enable, main_2_ram_read, main_2_ram_write, main_2_register_write;
  wire [1:0] main_1_state;
  wire [3:0] A, B, D, decoder_1_opcode, imm1, imm2, imm3, main_2_opcode_to_alu;
  wire [7:0] controlled_buffer_1_out, goto_imm, Instruction;
  wire [15:0] rom_1_data;
  wire [31:0] alu_1_output, n16_register_file_1_a, n16_register_file_1_b;

  Decoder decoder_1 (
    .Input(rom_1_data), .Destination_register(D), .opcode(decoder_1_opcode), .RegA(A), .RegB(B), .Imm2(imm2),
    .Imm1(imm1), .GoTo_Imm(goto_imm), .Imm3(imm3));
  ROM #(.dataWidth(16)) rom_1 (.addr(Instruction), .data(rom_1_data));  // open: sel
  assign controlled_buffer_1_out = Goto_enable ? goto_imm : 8'bz;  // Controlled_Buffer controlled_buffer_1
  _16_register_file u_16_register_file_1 (
    .d(alu_1_output), .Clk(main_2_register_write), .Rd(D), .Clr(Reset), .Ra(A), .Rb(B),
    .a(n16_register_file_1_a), .b(n16_register_file_1_b));
  Clock_main main_1 (
    .Increment_by(controlled_buffer_1_out), .Manual_Cycle(Manual_cycle), .Reset(Reset),
    .Counter(Instruction), .State(main_1_state));
  ALU alu_1 (
    .A(n16_register_file_1_a), .B(n16_register_file_1_b), .imm(goto_imm), .Op_code(main_2_opcode_to_alu),
    .in_5(main_2_alu_enable), .\output (alu_1_output));
  cliff_bus_control_11_07_15_main main_2 (
    .Cycle_LSB(main_1_state[0]), .Cycle_MSB(main_1_state[1]), .OP(decoder_1_opcode),
    .ALU_Enable(main_2_alu_enable), .Register_Write(main_2_register_write), .RAM_Read(main_2_ram_read),
    .RAM_Write(main_2_ram_write), .OPCode_to_ALU(main_2_opcode_to_alu), .Program_Counter_Update(Goto_enable));
  RAM #(.dataWidth(32), .bus("separate")) ram_1 (
    .data(alu_1_output), .str(main_2_ram_write), .ld(main_2_ram_read), .clr(Reset));  // open: addr, din, sel, clk

  // Notes on the sheet:
  //   ROM (Instructions)
  //   Clock
  //   Registers
  //   32-bit CPU
  //   By Cliff, Will, Tom, & Crissy
  //   ALU
  //   Bus Control
  //   RAM
endmodule
